// Logisim project LogisimLab6.circ as structural Verilog: 2 circuits, main circuit NextState
module NextState (
  input  Q2,
  input  Q1,
  input  Q0,
  input  X,
  output D2,
  output D1,
  output D0
);

  wire and_1_out, and_2_out, and_3_out, and_4_out, and_5_out, and_6_out, and_7_out, and_8_out, and_9_out,
       and_10_out, not_1_out, not_2_out, not_3_out, not_4_out, not_5_out, not_6_out, not_7_out;

  not not_1 (not_1_out, X);
  not not_2 (not_2_out, Q2);
  not not_3 (not_3_out, Q0);
  not not_4 (not_4_out, X);
  and and_1 (and_1_out, Q2, not_1_out);
  and and_2 (and_2_out, Q0, X);
  and and_3 (and_3_out, not_3_out, X);
  and and_4 (and_4_out, and_2_out, Q1);
  and and_5 (and_5_out, Q1, not_5_out);
  not not_5 (not_5_out, X);
  and and_6 (and_6_out, Q1, not_6_out);
  not not_6 (not_6_out, Q0);
  and and_7 (and_7_out, Q0, X);
  or or_1 (D2, and_1_out, and_4_out);
  not not_7 (not_7_out, Q1);
  and and_8 (and_8_out, not_2_out, and_3_out);
  and and_9 (and_9_out, Q0, not_4_out);
  and and_10 (and_10_out, not_7_out, and_7_out);
  or or_2 (D0, and_8_out, and_9_out);
  or or_3 (D1, and_5_out, and_6_out, and_10_out);
endmodule

module Main (
  input  X,
  input  Clear,
  output out_3,
  output [2:0] X3,
  output out_5,
  output [2:0] X3_2,
  output out_7
);

  wire clock_1_out, NextState_d0, NextState_d1, NextState_d2;

  Clock clock_1 (.out(clock_1_out));
  NextState NextState (
    .Q2(out_3), .Q1(out_5), .Q0(out_7), .X(X), .D2(NextState_d2), .D1(NextState_d1), .D0(NextState_d0));
  D_Flip_Flop D2 (.clk(clock_1_out), .D(NextState_d2), .Q(out_3), .reset(Clear));  // open: Qn, preset, en
  D_Flip_Flop D1 (.clk(clock_1_out), .D(NextState_d1), .Q(out_5), .reset(Clear));  // open: Qn, preset, en
  D_Flip_Flop D0 (.clk(clock_1_out), .D(NextState_d0), .Q(out_7), .reset(Clear));  // open: Qn, preset, en

  assign X3 = {out_3, out_5, out_7};
  assign X3_2 = {out_3, out_5, out_7};
endmodule
